# Fritzing sketch esp32-env-monitor (saved by Fritzing 0.9.3b)

parts:
  M1 = DOIT Esp32 DevKit v1 (30 pins long, 11 pins width) [part_number=ESP32S-PIN30]
  Part2 = Adafruit SGP30 Gas Sensor
  Part3 = Barometric Pressure Sensor - BMP180 Breakout (GY-68)
  WaveShare_1_3inch_OLED_128x1 = WaveShare 1.3inch OLED 128x64

nets:
  VCC: M1.3V3, Part2.VIN, Part3.VCC, WaveShare_1_3inch_OLED_128x1.VCC
  GND: M1.GND, Part2.GND, Part3.GND, WaveShare_1_3inch_OLED_128x1.GND
  N1: M1.RX2, WaveShare_1_3inch_OLED_128x1.RES
  N2: M1.TX2, WaveShare_1_3inch_OLED_128x1.CS
  N3: M1.D18, WaveShare_1_3inch_OLED_128x1.CLK
  N4: M1.D21, Part2.SDA, Part3.SDA
  N5: M1.RX0, WaveShare_1_3inch_OLED_128x1.D/C
  N6: M1.D22, Part2.SCL, Part3.SCL
  N7: M1.D23, WaveShare_1_3inch_OLED_128x1.DIN

custom parts:
  DOIT Esp32 DevKit v1 (30 pins long, 11 pins width): The DOIT Esp32 DevKit v1 is one of the development board created by DOIT to evaluate the ESP-WROOM-32 module. It is based on the ESP32 microcontroller that boasts Wifi, Bluetooth, Ethernet and Low Power support all in a single chip. (vanepp) made breadboard work, adjusted pin numbering and labels and reduced size of schematic and cleaned up pcb. This chip is 30pins long (2 x15) and 11 pins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
  WaveShare 1.3inch OLED 128x64: OLED Original design by Simulz (http://tsblog.simulz.kr) Corrected PCB layout by Andreas Horneffer
